# Fritzing sketch WiFi_Signal_ESP8622_v0 (saved by Fritzing 0.9.2b)
breadboards: 1

parts:
  WeMos_D1_Mini1 = WeMos D1 Mini
  LCD2 = LCD screen
  LCM1602_IIC2 = LCM1602 IIC [part_number="LCM1602 IIC" chip_label="LCM1602 IIC" package="DIP (Dual Inline) [THT]"]

nets:
  5V: WeMos_D1_Mini1.5V, LCM1602_IIC2.VCC
  N1: WeMos_D1_Mini1.D1, LCM1602_IIC2.SCL
  N2: WeMos_D1_Mini1.D2, LCM1602_IIC2.SDA
  N3: WeMos_D1_Mini1.G, LCM1602_IIC2.GND
  VSS: LCD2.VSS, LCM1602_IIC2.VSS
  VDD: LCD2.VDD, LCM1602_IIC2.VDD
  N4: LCD2.V0, LCM1602_IIC2.V0
  N5: LCD2.RS, LCM1602_IIC2.RS
  N6: LCD2.R/W, LCM1602_IIC2.RW
  N7: LCD2.E, LCM1602_IIC2.E
  N8: LCD2.DB0, LCM1602_IIC2.D0
  N9: LCD2.DB1, LCM1602_IIC2.D1
  N10: LCD2.DB2, LCM1602_IIC2.D2
  N11: LCD2.DB3, LCM1602_IIC2.D3
  N12: LCD2.DB4, LCM1602_IIC2.D4
  N13: LCD2.DB5, LCM1602_IIC2.D5
  N14: LCD2.DB6, LCM1602_IIC2.D6
  N15: LCD2.DB7, LCM1602_IIC2.D7
  N16: LCD2.LED+, LCM1602_IIC2.A
  N17: LCD2.LED-, LCM1602_IIC2.K
  N18: LCM1602_IIC2.LED_A, LCM1602_IIC2.LED_B

notes:
  Using 20 X 4 Display
  with integrated i2c driver.
  Dcreen address :0x3f
  http://r.ebay.com/ERz3Gl

custom parts:
  WeMos D1 Mini: The D1 mini is a mini wifi board based on ESP-8266EX.
  LCM1602 IIC: I2C-Module to use a 1602 or 2004 LCD on with the wire.h libory Serial LCD Modul
